# Fritzing sketch 2011 PMR Board Schematic rev02 (saved by Fritzing 0.9.3b)
breadboards: 1

parts:
  MV1 = MicroView [part_number=MicroView package="16pin wide"]
  VCC1 = Battery block 9V
  U1 = Voltage Regulator [package=to220-igo]
  R1 = Resistor [tolerance=±5% resistance=10k package=THT]
  R2 = Resistor [tolerance=±5% resistance=10k package=THT]
  L1 = Solenoid
  Q1 = Basic FET N-Channel [package="DPak [SMD]"]
  2_2mF = Electrolytic Capacitor [capacitance=1mF voltage=10V package="100 mil [THT, electrolytic]"]
  C4 = Electrolytic Capacitor [capacitance=10µF package="100 mil [THT, electrolytic]"]
  C5 = Electrolytic Capacitor [capacitance=10µF package="100 mil [THT, electrolytic]"]
  C6 = Ceramic Capacitor [capacitance=1µF package="100 mil [THT, multilayer]"]
  R3 = Resistor [tolerance=±5% resistance=10k package=THT]
  Down = Pushbutton [package=THT]
  Up = Pushbutton [package=THT]
  Trigger = Toggle Switch [package=THT]
  LED1 = LED - 5mm [color="Infrared (940nm)" package="5 mm [THT]"]
  R4 = Photocell (LDR) [package=THT]
  R5 = Resistor [tolerance=±5% resistance=220 package=THT]

nets:
  N1: MV1.A5, R1.Pin_1, R2.Pin_0
  N2: MV1.A2, R5.Pin_0
  N3: MV1.A1, R4.pin_0
  GND: MV1.GND, VCC1.-, U1.GND, R2.Pin_1, Q1.source, 2_2mF.-, C4.-, C5.-, C6.0, Down.leg0, Up.leg0, Trigger.L2, LED1.cathode, R4.pin_1
  N4: MV1.RXD, Trigger.COM
  N5: MV1.TXD, R3.Pin_0
  N6: MV1.D2, Down.leg1
  N7: MV1.D3, Up.leg1
  N8: MV1.Vin, U1.OUT, C5.+
  N9: VCC1.+, U1.IN, R1.Pin_0, L1.pin1, 2_2mF.+, C4.+
  N10: L1.pin2, Q1.drain
  N11: Q1.Gate, C6.1, R3.Pin_1
  N12: LED1.anode, R5.Pin_1

custom parts:
  MicroView: MicroView - Chip-sized Arduino with OLED display.
